// Digital circuit ELTN32-CORE.dig as structural Verilog
module ELTN32_CORE (
);

  wire _7408_3_pin3, _7408_3_pin6, _7408_3_pin8, _7408_3_pin10, _7408_6_pin3, _7408_6_pin6, BadState, BAND,
       BAND_t, ClearCounter, CounterReset, CounterReset_t, EC0, EC0__SC0, EC0_SC0,
       EC0_SC0__plus__EC0__plus_SC0, EC0_t, EC1, EC1__SC1, EC1_SC1, EC1_SC1__plus__EC1__plus_SC1, EC1_t, EC2,
       EC2__SC2, EC2_SC2, EC2_SC2__plus__EC2__plus_SC2, EC2_t, EC3, EC3__SC3, EC3_SC3,
       EC3_SC3__plus__EC3__plus_SC3, EC3_t, EC4, EC4__SC4, EC4_SC4, EC4_SC4__plus__EC4__plus_SC4, EC4_t, EC5,
       EC5__SC5, EC5_SC5, EC5_SC5__plus__E51__plus_SC5, EC5_t, EC6, EC6__SC6, EC6_SC6,
       EC6_SC6__plus__EC6__plus_SC6, EC6_t, EC7, EC7__SC7, EC7_SC7, EC7_SC7__plus__EC7__plus_SC7, EC7_t,
       Enabled, EnterBtn, GAND, GAND_t, GlobalStop, GlobalStop_plus_BadEntry, GlobalStop_plus_BadEntry_t,
       IS5, IsLocked, IsMatch, IsMatch_t, KillSignalForYellow, KillSignalForYellow_t, QA, QB, QC, ResetBtn,
       ResetBtn_t, SC0, SC0_t, SC1, SC1_t, SC2, SC2_t, SC3, SC3_t, SC4, SC4_t, SC5, SC5_t, SC6, SC6_t, SC7,
       SC7_t, UnlockState;

  Button ENTER (.out(EnterBtn));
  Button RESET (.out(ResetBtn));
  LED UNLOCKED (.in(UnlockState));
  LED BAD_CODE (.in(KillSignalForYellow));
  LED LOCKED_OUT (.in(IsLocked));
  DipSwitch #(.Bits(8)) u_EC1 (.out(EC0));
  DipSwitch u_EC2 (.out(EC1));
  DipSwitch u_EC3 (.out(EC2));
  DipSwitch u_EC4 (.out(EC3));
  DipSwitch u_EC5 (.out(EC4));
  DipSwitch u_EC6 (.out(EC5));
  DipSwitch u_EC7 (.out(EC6));
  DipSwitch EC8 (.out(EC7));
  DipSwitch #(.dipDefault("true"), .Bits(8)) u_SC1 (.out(SC0));
  DipSwitch u_SC2 (.out(SC1));
  DipSwitch u_SC3 (.out(SC2));
  DipSwitch u_SC4 (.out(SC3));
  DipSwitch u_SC5 (.out(SC4));
  DipSwitch u_SC6 (.out(SC5));
  DipSwitch u_SC7 (.out(SC6));
  DipSwitch SC8 (.out(SC7));
  Seven_Seg_Hex seven_seg_hex_1 (.d({1'b0, QC, QB, QA}), .dp(1'b1));
  _7404 _7404_1 (
    .pin1(EC0), .pin2(EC0_t), .pin3(EC1), .pin4(EC1_t), .pin5(EC2), .pin6(EC2_t), .pin7(1'b0), .pin8(EC3_t),
    .pin9(EC3), .pin10(EC4_t), .pin11(EC4), .pin12(EC5_t), .pin13(EC5), .pin14(1'b1));
  _7404 _7404_2 (
    .pin1(EC6), .pin2(EC6_t), .pin3(EC7), .pin4(EC7_t), .pin5(SC0), .pin6(SC0_t), .pin7(1'b0), .pin8(SC1_t),
    .pin9(SC1), .pin10(SC2_t), .pin11(SC2), .pin12(SC3_t), .pin13(SC3), .pin14(1'b1));
  _7404 _7404_3 (
    .pin1(SC4), .pin2(SC4_t), .pin3(SC5), .pin4(SC5_t), .pin5(SC6), .pin6(SC6_t), .pin7(1'b0),
    .pin8(IsLocked), .pin9(IS5), .pin10(IsMatch_t), .pin11(IsMatch), .pin12(SC7_t), .pin13(SC7), .pin14(1'b1));
  _7404 _7404_4 (
    .pin1(GAND), .pin2(GAND_t), .pin3(ResetBtn), .pin4(ResetBtn_t), .pin5(BAND), .pin6(BAND_t), .pin7(1'b0),
    .pin8(KillSignalForYellow_t), .pin9(KillSignalForYellow), .pin10(GlobalStop_plus_BadEntry_t),
    .pin11(GlobalStop_plus_BadEntry), .pin12(CounterReset_t), .pin13(CounterReset), .pin14(1'b1));
  _7408 _7408_1 (
    .pin1(EC0), .pin2(SC0), .pin3(EC0_SC0), .pin4(SC0_t), .pin5(EC0_t), .pin6(EC0__SC0), .pin7(1'b0),
    .pin8(EC1__SC1), .pin9(SC1_t), .pin10(EC1_t), .pin11(EC1_SC1), .pin12(SC1), .pin13(EC1), .pin14(1'b1));
  _7408 _7408_2 (
    .pin1(EC4), .pin2(SC4), .pin3(EC4_SC4), .pin4(SC4_t), .pin5(EC4_t), .pin6(EC4__SC4), .pin7(1'b0),
    .pin8(EC5__SC5), .pin9(SC5_t), .pin10(EC5_t), .pin11(EC5_SC5), .pin12(SC5), .pin13(EC5), .pin14(1'b1));
  _7408 _7408_3 (
    .pin1(EC0_SC0__plus__EC0__plus_SC0), .pin2(EC1_SC1__plus__EC1__plus_SC1), .pin3(_7408_3_pin3),
    .pin4(_7408_3_pin3), .pin5(EC2_SC2__plus__EC2__plus_SC2), .pin6(_7408_3_pin6), .pin7(1'b0),
    .pin8(_7408_3_pin8), .pin9(EC4_SC4__plus__EC4__plus_SC4), .pin10(_7408_3_pin10), .pin11(_7408_3_pin10),
    .pin12(EC3_SC3__plus__EC3__plus_SC3), .pin13(_7408_3_pin6), .pin14(1'b1));
  _7408 _7408_4 (
    .pin1(EC2), .pin2(SC2), .pin3(EC2_SC2), .pin4(SC2_t), .pin5(EC2_t), .pin6(EC2__SC2), .pin7(1'b0),
    .pin8(EC3__SC3), .pin9(SC3_t), .pin10(EC3_t), .pin11(EC3_SC3), .pin12(SC3), .pin13(EC3), .pin14(1'b1));
  _7408 _7408_5 (
    .pin1(EC6), .pin2(SC6), .pin3(EC6_SC6), .pin4(SC6_t), .pin5(EC6_t), .pin6(EC6__SC6), .pin7(1'b0),
    .pin8(EC7__SC7), .pin9(SC7_t), .pin10(EC7_t), .pin11(EC7_SC7), .pin12(SC7), .pin13(EC7), .pin14(1'b1));
  _7408 _7408_6 (
    .pin1(_7408_3_pin8), .pin2(EC5_SC5__plus__E51__plus_SC5), .pin3(_7408_6_pin3), .pin4(_7408_6_pin3),
    .pin5(EC6_SC6__plus__EC6__plus_SC6), .pin6(_7408_6_pin6), .pin7(1'b0), .pin8(1'b0), .pin9(1'b0),
    .pin10(1'b0), .pin11(IsMatch), .pin12(EC7_SC7__plus__EC7__plus_SC7), .pin13(_7408_6_pin6), .pin14(1'b1));
  _7432 _7432_1 (
    .pin1(EC0_SC0), .pin2(EC0__SC0), .pin3(EC0_SC0__plus__EC0__plus_SC0), .pin4(EC1_SC1), .pin5(EC1__SC1),
    .pin6(EC1_SC1__plus__EC1__plus_SC1), .pin7(1'b0), .pin8(EC3_SC3__plus__EC3__plus_SC3), .pin9(EC3__SC3),
    .pin10(EC3_SC3), .pin11(EC2_SC2__plus__EC2__plus_SC2), .pin12(EC2__SC2), .pin13(EC2_SC2), .pin14(1'b1));
  _7432 _7432_2 (
    .pin1(EC4_SC4), .pin2(EC4__SC4), .pin3(EC4_SC4__plus__EC4__plus_SC4), .pin4(EC5_SC5), .pin5(EC5__SC5),
    .pin6(EC5_SC5__plus__E51__plus_SC5), .pin7(1'b0), .pin8(EC7_SC7__plus__EC7__plus_SC7), .pin9(EC7__SC7),
    .pin10(EC7_SC7), .pin11(EC6_SC6__plus__EC6__plus_SC6), .pin12(EC6__SC6), .pin13(EC6_SC6), .pin14(1'b1));
  _7442 _7442_1 (
    .pin6(IS5), .pin8(1'b0), .pin12(1'b0), .pin13(QC), .pin14(QB), .pin15(QA), .pin16(1'b1));  // open: pin1, pin2, pin3, pin4, pin5, pin7, pin9, pin10, pin11
  _74193 _74193_1 (
    .pin1(1'b0), .pin2(QB), .pin3(QA), .pin4(1'b1), .pin5(BAND), .pin6(QC), .pin8(1'b0), .pin9(1'b0),
    .pin10(1'b0), .pin11(1'b1), .pin14(CounterReset), .pin15(1'b0), .pin16(1'b1));  // open: pin7, pin12, pin13
  _7432 _7432_3 (
    .pin1(ResetBtn), .pin2(IsLocked), .pin3(GlobalStop), .pin4(GlobalStop), .pin5(BAND),
    .pin6(GlobalStop_plus_BadEntry), .pin7(1'b0), .pin8(KillSignalForYellow),
    .pin9(GlobalStop_plus_BadEntry), .pin10(ResetBtn), .pin11(CounterReset), .pin12(GAND), .pin13(ResetBtn),
    .pin14(1'b1));
  _7408 _7408_7 (
    .pin1(EnterBtn), .pin2(IS5), .pin3(Enabled), .pin4(Enabled), .pin5(IsMatch_t), .pin6(BAND), .pin7(1'b0),
    .pin8(GAND), .pin9(Enabled), .pin10(IsMatch), .pin11(ClearCounter), .pin12(GAND), .pin13(ResetBtn),
    .pin14(1'b1));
  _7474 _7474_1 (
    .pin1(GlobalStop_plus_BadEntry_t), .pin2(1'b0), .pin3(1'b0), .pin4(GAND_t), .pin5(UnlockState),
    .pin7(1'b0), .pin9(BadState), .pin10(GAND), .pin11(CounterReset_t), .pin12(1'b0),
    .pin13(KillSignalForYellow_t), .pin14(1'b1));  // open: pin6, pin8

  // Notes on the sheet:
  //   ENTRY CODE (EC)
  //   SECRET CODE (SC)
  //   7404
  //   Hex Inverter
  //   EC0-EC5
  //   7404
  //   Hex Inverter
  //   EC6-EC7
  //   SC1-SC3
  //   7404
  //   Hex Inverter
  //   SC4-SC7
  //   7408 - AND 
  //   EC0 & SC0, EC0' & SC0'
  //   EC1 & SC1, EC1' & SC1'
  //   7408 - AND
  //   EC4 & SC4, EC4' & SC4'
  //   EC5 & SC5, EC5' & SC5'
  //   7408 - AND
  //   EC2 & SC2, EC2' & SC2'
  //   EC3 & SC3, EC3' & SC3'
  //   7408 - AND
  //   EC6 & SC6, EC6' & SC6'
  //   EC7 & SC7, EC7' & SC7'
  //   IsMatch
  //   2X 7408 AND 
  //   (EC0&SC0)+(EC0'+SC0') & (EC1&SC1)+(EC1'+SC1') & 
  //   (EC2&SC2)+(EC2'+SC2') & (EC3&SC3)+(EC3'+SC3') & 
  //   (EC4&SC4)+(EC4'+SC4') & (EC5&SC5)+(E51'+SC5') & 
  //   (EC6&SC6)+(EC6'+SC6') & (EC7&SC7)+(EC7'+SC7')
  //   7432 Quad 2 Input OR
  //   (EC0&SC0)+(EC0'+SC0')
  //   (EC1&SC1)+(EC1'+SC1')
  //   (EC2&SC2)+(EC2'+SC2')
  //   (EC3&SC3)+(EC3'+SC3')
  //   7432 Quad 2 Input OR
  //   (EC4&SC4)+(EC4'+SC4')
  //   (EC5&SC5)+(E51'+SC5')
  //   (EC6&SC6)+(EC6'+SC6')
  //   (EC7&SC7)+(EC7'+SC7')
  //   7442 (BCD to Decimal Decoder)
  //   74193 (4-bit Up/Down Counter)
  //   Turn off Yellow because of a change in state.
  //   7432 Quad 2 Input OR
  //   7474 (Dual D-Type Flip-Flop)
endmodule
